# Fritzing sketch 3WDTrashBase (saved by Fritzing 0.9.5d)

parts:
  VCC1 = Battery
  DC_Mot_Enc1 = DC Motor with two-phase hall-encoder [part_number=VT-E-G25A-06-177E]
  DC_Mot_Enc3 = DC Motor with two-phase hall-encoder [part_number=VT-E-G25A-06-177E]
  Mod1 = Raspberry Pi 4B
  DC_Mot_Enc5 = DC Motor with two-phase hall-encoder [part_number=VT-E-G25A-06-177E]
  S1 = H-Bridge with L298N
  S2 = H-Bridge with L298N

nets:
  GND: VCC1.-, DC_Mot_Enc1.pin5, DC_Mot_Enc3.pin5, DC_Mot_Enc5.pin5, S1.GND, S2.GND
  12V: VCC1.+, S1.12V, S2.12V
  N1: DC_Mot_Enc1.pin1, S2.M1-01
  N2: DC_Mot_Enc1.pin2, S2.5V
  N3: DC_Mot_Enc1.pin3, Mod1.GPIO20
  N4: DC_Mot_Enc1.pin4, Mod1.GPIO21
  N5: DC_Mot_Enc1.pin6, S2.M1-02
  N6: DC_Mot_Enc3.pin1, S1.M1-01
  N7: DC_Mot_Enc3.pin2, DC_Mot_Enc5.pin2, S1.5V
  N8: DC_Mot_Enc3.pin3, Mod1.GPIO6
  N9: DC_Mot_Enc3.pin4, Mod1.GPIO5
  N10: DC_Mot_Enc3.pin6, S1.M1-02
  N11: Mod1.GPIO2, S1.ENB
  N12: Mod1.GPIO3, S1.IN4
  N13: Mod1.GPIO4, S1.IN3
  N14: Mod1.GPIO14, S2.ENA
  N15: Mod1.GPIO15, S2.IN1
  N16: Mod1.GPIO17, S1.IN2
  N17: Mod1.GPIO18, S2.IN2
  N18: Mod1.GPIO27, S1.IN1
  N19: Mod1.GPIO22, S1.ENA
  N20: Mod1.GPIO13, DC_Mot_Enc5.pin4
  N21: Mod1.GPIO19, DC_Mot_Enc5.pin3
  N22: DC_Mot_Enc5.pin1, S1.M1-04
  N23: DC_Mot_Enc5.pin6, S1.M1-03

custom parts:
  Battery: Your standard 3x 18650 battery pack (12 Volts)
  H-Bridge with L298N: h-bridge
